# Fritzing sketch wedding_clock (saved by Fritzing 0.9.3b)
breadboards: 1

parts:
  Part1 = Arduino Uno (Rev3)
  SP1 = SPEAKER [package=pcb_mount_speaker]
  J1 = Basic Servo
  J2 = Basic Servo
  U1 = SWITCH_SPDT [package=kps-1290]
  J3 = Screw terminal - 2 pins [package=THT]
  part = Resistor [tolerance=±5% resistance=1M package="2512 [SMD]"]
  S1 = Round Pushbutton
  part_2 = Resistor [tolerance=±5% resistance=10k package="2512 [SMD]"]
  U2 = RELAY [package=relay-g5q]
  D1 = Diode [package=diode-1n4001]
  S2 = SWITCH-MOMENTARY-2 [package=reed_switch_plastic]
  R1 = Resistor [tolerance=±5% resistance=220 package="2512 [SMD]"]
  J4 = Screw terminal - 2 pins [package=THT]
  Q1 = NPN-Transistor [package="TO92 [THT]"]
  VCC2 = Battery
  DUMMY_BATTERY_(to_clock) = Battery Holders [package=battery-aa]
  U3 = Battery Holders [package=battery-aa]
  VCC1 = Battery

nets:
  N1: Part1.D9_PWM, J2.pulse
  N2: Part1.D10_PWM/SS, J1.pulse
  N3: Part1.D11_PWM/MOSI, SP1.-
  N4: Part1.D2, J3.pin2, part.Pin_1, S2.2
  N5: Part1.D3_PWM, S1.leg1, part_2.Pin_1
  N6: Part1.D4, R1.Pin_0
  5V: Part1.5V, part.Pin_0, part_2.Pin_0, U2.COIL1, D1.C
  GND: Part1.GND, SP1.+, J1.gnd, J2.gnd, J3.pin1, S1.leg0, S2.1, Q1.B, VCC2.-
  VCC: J1.vcc, J2.vcc, U1.P
  N7: U1.S, VCC1.+
  N8: U2.COIL2, D1.A, Q1.E
  N9: U2.MAIN, U3.+
  N10: U2.NO, J4.pin1, DUMMY_BATTERY_(to_clock).+
  N11: R1.Pin_1, Q1.C
  N12: J4.pin2, DUMMY_BATTERY_(to_clock).-, U3.-
  N13: VCC2.+, VCC1.-
